# Fritzing sketch bicigenerador (saved by Fritzing 0.8.0b)
breadboards: 1

parts:
  Parte1 = Arduino Uno (Rev3)
  Sharp_Sensor = screw terminal, 3 pins
  R1 = Resistor [tolerance=±5% resistance=10k package=THT]
  R2 = Resistor [tolerance=±5% resistance=10 package=THT]
  U1 = RF Transmitter [package=THT]
  REF_GND = screw terminal, 2 pins
  reed_switch = screw terminal, 2 pins

nets:
  N1: Parte1.A0, Sharp_Sensor.pin3
  N2: Parte1.GND, Sharp_Sensor.pin2, R1.Pin_1, R2.Pin_1, U1.pin1
  N3: Parte1.D2, R1.Pin_0, reed_switch.pin2
  N4: Parte1.D3_PWM, U1.pin2
  N5: Parte1.5V, Sharp_Sensor.pin1, U1.pin3, reed_switch.pin1
  N6: R2.Pin_0, REF_GND.pin1, REF_GND.pin2

notes:
  Luz & Fuerza
  Bicigenerador
  2013

custom parts:
  RF Transmitter: Transmitter for RWS 371 receiver
