# Fritzing sketch frankitropo (saved by Fritzing 0.8.0b)
breadboards: 1

parts:
  U1 = RWS-371 [package=THT]
  Parte1 = Arduino Uno (Rev3)
  J2 = Screw terminal - 2 pins [package=THT]
  J3 = Screw terminal - 2 pins [package=THT]
  J4 = Screw terminal - 2 pins [package=THT]
  J5 = Screw terminal - 2 pins [package=THT]
  R1 = Rotary Potentiometer (Large) [maximum_resistance=100kΩ package=THT]
  J6 = Screw terminal - 2 pins [package=THT]
  J1 = Screw terminal - 2 pins [package=THT]

nets:
  N1: U1.pin1, U1.pin_6, U1.pin_7, Parte1.GND, R1.leg1
  N2: U1.pin2, Parte1.D1/TX
  N3: U1.pin_4, U1.pin_5, Parte1.5V, R1.leg2
  N4: Parte1.A0, R1.wiper
  N5: Parte1.D8, J3.pin2
  N6: Parte1.D9_PWM, J3.pin1
  N7: Parte1.D10_PWM/SS, J2.pin2
  N8: Parte1.D11_PWM/MOSI, J2.pin1
  N9: Parte1.D12/MISO, J1.pin2
  N10: Parte1.D13/SCK, J1.pin1
  N11: Parte1.D2, J6.pin2
  N12: Parte1.D3_PWM, J6.pin1
  N13: Parte1.D4, J5.pin2
  N14: Parte1.D5_PWM, J5.pin1
  N15: Parte1.D6_PWM, J4.pin2
  N16: Parte1.D7, J4.pin1

notes:
  Luz & Fuerza
  frankitropo
  2013
  1-2
  3-4
  5-6
  7-8
  9-10
  11-12
  receiver
  antenna
  pot

custom parts:
  RWS-371: RF Receiver
